// Logisim project Q1.circ as structural Verilog: 9 circuits, main circuit main
module main (
);

  // AND_Gate and_1 is placed but not wired
endmodule

module AND_Gate_Q_1 (
  input  A,
  input  B,
  output C
);

  and and_1 (C, A, B);
endmodule

module Not_Gate_Q1__2 (
  input  A,
  output B
);

  not not_1 (B, A);
endmodule

module OR_Gate_Q1_3 (
  input  in_1,
  input  in_2,
  output out_3
);

  or or_1 (out_3, in_1, in_2);
endmodule

module NOR_Gate_Q1_4 (
  input  A,
  input  B,
  output C
);

  nor nor_1 (C, A, B);
endmodule

module NAND_Gate_Q1_5 (
  input  A,
  input  B,
  output C
);

  nand nand_1 (C, A, B);
endmodule

module EX_OR_Gate_Q1_6 (
  input  in_1,
  input  in_2,
  output out_3
);

  ExactlyOne xor_1 (.out(out_3), .in0(in_1), .in1(in_1), .in4(in_2));
endmodule

module Q2_Implementing_NOT_using_NAND_Gate (
  output [1:0] A,
  output out_2,
  output A_B__prime__prime_A_B,
  output [1:0] B
);

  nand nand_1 (out_2, A[0], B[0]);
  nand nand_2 (A_B__prime__prime_A_B, out_2, out_2);
  // Pins of 1 and 2 bits meet at A
  // Pins of 1 and 2 bits meet at B

  // Notes on the sheet:
  //   (A,B)
endmodule

module _2_b (
  output [1:0] out_1,
  output out_2
);

  nand nand_1 (out_2, out_1[0], out_1[0]);
  // Pins of 1 and 2 bits meet at out_1
endmodule
